# Fritzing sketch Electric Realistic Design RCS (saved by Fritzing 0.9.6b)
breadboards: 1

parts:
  Pololu_A1 = Pololu A4988 [package=SO16]
  Pololu_A2 = Pololu A4988 [package=SO16]
  Pololu_A3 = Pololu A4988 [package=SO16]
  Pololu_A4 = Pololu A4988 [package=SO16]
  Pololu_A5 = Pololu A4988 [package=SO16]
  Pololu_A6 = Pololu A4988 [package=SO16]
  Componente1 = Arduino Mega Proto Shield
  M1 = Stepper Motor - Bipolar
  M2 = Stepper Motor - Bipolar
  M3 = Stepper Motor - Bipolar
  M4 = Stepper Motor - Bipolar
  M5 = Stepper Motor - Bipolar
  M6 = Stepper Motor - Bipolar
  C5 = Electrolytic Capacitor [capacitance=1000μF voltage=35V package="1010 [SMD, electrolytic]"]
  C6 = Electrolytic Capacitor [capacitance=1000μF voltage=35V package="1010 [SMD, electrolytic]"]
  C7 = Electrolytic Capacitor [capacitance=1000μF voltage=35V package="1010 [SMD, electrolytic]"]
  C8 = Electrolytic Capacitor [capacitance=1000μF voltage=35V package="1010 [SMD, electrolytic]"]
  C9 = Electrolytic Capacitor [capacitance=1000μF voltage=35V package="1010 [SMD, electrolytic]"]
  C10 = Electrolytic Capacitor [capacitance=1000μF voltage=35V package="1010 [SMD, electrolytic]"]
  Power_plug1 = Power plug

nets:
  N1: Pololu_A1.ENABLE, Componente1.D23
  N2: Pololu_A1.RESET, Pololu_A1.SLEEP
  N3: Pololu_A1.STEP, Componente1.D50
  N4: Pololu_A1.DIR, Componente1.D52
  GND: Pololu_A1.GND, Pololu_A2.GND, Pololu_A3.GND, Pololu_A4.GND, Pololu_A5.GND, Pololu_A6.GND, Componente1.GND, C5.-, C6.-, C7.-, C8.-, C9.-, C10.-, Power_plug1.GND
  VDD: Pololu_A1.VDD, Pololu_A2.VDD, Pololu_A3.VDD, Pololu_A4.VDD, Pololu_A5.VDD, Pololu_A6.VDD, Componente1.5V
  N5: Pololu_A1.1B, M1.D
  N6: Pololu_A1.1A, M1.B
  N7: Pololu_A1.2A, M1.C
  N8: Pololu_A1.2B, M1.A
  N9: Pololu_A1.VMOT, Pololu_A2.VMOT, Pololu_A3.VMOT, Pololu_A4.VMOT, Pololu_A5.VMOT, Pololu_A6.VMOT, C5.+, C6.+, C7.+, C8.+, C9.+, C10.+, Power_plug1.VCC
  N10: Pololu_A2.ENABLE, Componente1.D43
  N11: Pololu_A2.RESET, Pololu_A2.SLEEP
  N12: Pololu_A2.STEP, Componente1.D30
  N13: Pololu_A2.DIR, Componente1.D32
  N14: Pololu_A2.1B, M6.D
  N15: Pololu_A2.1A, M6.B
  N16: Pololu_A2.2A, M6.C
  N17: Pololu_A2.2B, M6.A
  N18: Pololu_A3.ENABLE, Componente1.D39
  N19: Pololu_A3.RESET, Pololu_A3.SLEEP
  N20: Pololu_A3.STEP, Componente1.D34
  N21: Pololu_A3.DIR, Componente1.D36
  N22: Pololu_A3.1B, M5.D
  N23: Pololu_A3.1A, M5.B
  N24: Pololu_A3.2A, M5.C
  N25: Pololu_A3.2B, M5.A
  N26: Pololu_A4.ENABLE, Componente1.D35
  N27: Pololu_A4.RESET, Pololu_A4.SLEEP
  N28: Pololu_A4.STEP, Componente1.D38
  N29: Pololu_A4.DIR, Componente1.D40
  N30: Pololu_A4.1B, M4.D
  N31: Pololu_A4.1A, M4.B
  N32: Pololu_A4.2A, M4.C
  N33: Pololu_A4.2B, M4.A
  N34: Pololu_A5.ENABLE, Componente1.D31
  N35: Pololu_A5.RESET, Pololu_A5.SLEEP
  N36: Pololu_A5.STEP, Componente1.D42
  N37: Pololu_A5.DIR, Componente1.D44
  N38: Pololu_A5.1B, M3.D
  N39: Pololu_A5.1A, M3.B
  N40: Pololu_A5.2A, M3.C
  N41: Pololu_A5.2B, M3.A
  N42: Pololu_A6.ENABLE, Componente1.D27
  N43: Pololu_A6.RESET, Pololu_A6.SLEEP
  N44: Pololu_A6.STEP, Componente1.D46
  N45: Pololu_A6.DIR, Componente1.D48
  N46: Pololu_A6.1B, M2.D
  N47: Pololu_A6.1A, M2.B
  N48: Pololu_A6.2A, M2.C
  N49: Pololu_A6.2B, M2.A
