# Fritzing sketch Electric Scheme RCS (saved by Fritzing 0.9.6b)
breadboards: 1

parts:
  BACK_MOTOR = Stepper Motor - Bipolar
  Pololu_A1 = Pololu A4988 [package=SO16]
  C8 = Electrolytic Capacitor [capacitance=1000μF voltage=35V package="1010 [SMD, electrolytic]"]
  UP_MOTOR = Stepper Motor - Bipolar
  Pololu_A2 = Pololu A4988 [package=SO16]
  C9 = Electrolytic Capacitor [capacitance=1000μF voltage=35V package="1010 [SMD, electrolytic]"]
  FRONT_MOTOR = Stepper Motor - Bipolar
  Pololu_A3 = Pololu A4988 [package=SO16]
  C10 = Electrolytic Capacitor [capacitance=1000μF voltage=35V package="1010 [SMD, electrolytic]"]
  LEFT_MOTOR = Stepper Motor - Bipolar
  Pololu_A4 = Pololu A4988 [package=SO16]
  C11 = Electrolytic Capacitor [capacitance=1000μF voltage=35V package="1010 [SMD, electrolytic]"]
  RIGHT_MOTOR = Stepper Motor - Bipolar
  Pololu_A5 = Pololu A4988 [package=SO16]
  C12 = Electrolytic Capacitor [capacitance=1000μF voltage=35V package="1010 [SMD, electrolytic]"]
  DOWN_MOTOR = Stepper Motor - Bipolar
  Pololu_A6 = Pololu A4988 [package=SO16]
  C13 = Electrolytic Capacitor [capacitance=1000μF voltage=35V package="1010 [SMD, electrolytic]"]
  Componente1 = Arduino Mega Proto Shield
  Power_plug1 = Power plug

nets:
  N1: BACK_MOTOR.A, Pololu_A1.2B
  N2: BACK_MOTOR.C, Pololu_A1.2A
  N3: BACK_MOTOR.B, Pololu_A1.1A
  N4: BACK_MOTOR.D, Pololu_A1.1B
  N5: Pololu_A1.ENABLE, Componente1.D48
  N6: Pololu_A1.RESET, Pololu_A1.SLEEP
  N7: Pololu_A1.STEP, Componente1.D40
  N8: Pololu_A1.DIR, Componente1.D38
  GND: Pololu_A1.GND, C8.-, Pololu_A2.GND, C9.-, Pololu_A3.GND, C10.-, Componente1.GND, Power_plug1.GND
  VDD: Pololu_A1.VDD, Pololu_A2.VDD, Pololu_A3.VDD, Pololu_A4.VDD, Pololu_A5.VDD, Pololu_A6.VDD, Componente1.5V
  N9: Pololu_A1.VMOT, C8.+, Pololu_A2.VMOT, C9.+
  N10: UP_MOTOR.A, Pololu_A2.2B
  N11: UP_MOTOR.C, Pololu_A2.2A
  N12: UP_MOTOR.B, Pololu_A2.1A
  N13: UP_MOTOR.D, Pololu_A2.1B
  N14: Pololu_A2.ENABLE, Componente1.D35
  N15: Pololu_A2.RESET, Pololu_A2.SLEEP
  N16: Pololu_A2.STEP, Componente1.D34
  N17: Pololu_A2.DIR, Componente1.D36
  N18: FRONT_MOTOR.A, Pololu_A3.2B
  N19: FRONT_MOTOR.C, Pololu_A3.2A
  N20: FRONT_MOTOR.B, Pololu_A3.1A
  N21: FRONT_MOTOR.D, Pololu_A3.1B
  N22: Pololu_A3.ENABLE, Componente1.D27
  N23: Pololu_A3.RESET, Pololu_A3.SLEEP
  N24: Pololu_A3.STEP, Componente1.D26
  N25: Pololu_A3.DIR, Componente1.D28
  N26: Pololu_A3.VMOT, C10.+, Pololu_A4.VMOT, C11.+, Pololu_A5.VMOT, C12.+, Pololu_A6.VMOT, C13.+, Power_plug1.VCC
  N27: LEFT_MOTOR.A, Pololu_A4.2B
  N28: LEFT_MOTOR.C, Pololu_A4.2A
  N29: LEFT_MOTOR.B, Pololu_A4.1A
  N30: LEFT_MOTOR.D, Pololu_A4.1B
  N31: Pololu_A4.ENABLE, Componente1.D52
  N32: Pololu_A4.RESET, Pololu_A4.SLEEP
  N33: Pololu_A4.STEP, Componente1.D44
  N34: Pololu_A4.DIR, Componente1.D42
  GND_2: Pololu_A4.GND, C11.-, Pololu_A5.GND, C12.-, Pololu_A6.GND, C13.-
  N35: RIGHT_MOTOR.A, Pololu_A5.2B
  N36: RIGHT_MOTOR.C, Pololu_A5.2A
  N37: RIGHT_MOTOR.B, Pololu_A5.1A
  N38: RIGHT_MOTOR.D, Pololu_A5.1B
  N39: Pololu_A5.ENABLE, Componente1.D30
  N40: Pololu_A5.RESET, Pololu_A5.SLEEP
  N41: Pololu_A5.STEP, Componente1.D31
  N42: Pololu_A5.DIR, Componente1.D46
  N43: DOWN_MOTOR.A, Pololu_A6.2B
  N44: DOWN_MOTOR.C, Pololu_A6.2A
  N45: DOWN_MOTOR.B, Pololu_A6.1A
  N46: DOWN_MOTOR.D, Pololu_A6.1B
  N47: Pololu_A6.ENABLE, Componente1.D22
  N48: Pololu_A6.RESET, Pololu_A6.SLEEP
  N49: Pololu_A6.STEP, Componente1.D23
